# Fritzing sketch Schematic (saved by Fritzing 0.9.10b)
breadboards: 1

parts:
  J1 = STM32 Nucleo boards
  IC1 = IC, DIP package, 8 pins [chip_label=DS1631]
  IC2 = IC, DIP package, 16 pins [chip_label=74HC595N]
  LCD1 = LCD screen
  R1 = Resistor [tolerance=±5% resistance=220 package="0805 [SMD]"]
  R2 = Resistor [tolerance=±5% resistance=220 package="0805 [SMD]"]

nets:
  N1: J1.D10_PWM/SS, IC2.pin12
  N2: J1.D11_PWM/MOSI, IC2.pin14
  N3: J1.D13/SCK, IC2.pin11
  N4: J1.A4/SDA, IC1.pin1, R2.Pin_0
  N5: J1.A5/SCL, IC1.pin2, R1.Pin_0
  3V3: J1.3V3, LCD1.VDD
  N6: J1.5V, IC1.pin8, IC2.pin10, IC2.pin16, LCD1.LED+, R1.Pin_1, R2.Pin_1
  GND: J1.GND, IC1.pin5, IC1.pin6, IC1.pin7, IC2.pin13, LCD1.VSS, LCD1.R/W, LCD1.LED-
  N7: IC2.pin2, LCD1.RS
  N8: IC2.pin3, LCD1.E
  N9: IC2.pin4, LCD1.DB4
  N10: IC2.pin5, LCD1.DB5
  N11: IC2.pin6, LCD1.DB6
  N12: IC2.pin7, LCD1.DB7

notes:
  Purple: SPI Pins
  Yellow: I2C Pins
  Brown: D4-D7
  Orange: RS
  Blue: RW
  Green: E
  Grey: PWM Pins
